# Fritzing sketch button_circuit (saved by Fritzing 0.9.9b)
breadboards: 1

parts:
  Mod1 = Raspberry Pi 4B
  S1 = Pushbutton [package="[THT]"]
  R1 = Resistor [tolerance=±5% power=0.25 resistance=220 package=THT]

nets:
  N1: Mod1.3V3, R1.Pin_0
  N2: Mod1.GPIO4, S1.Pin_3, S1.Pin_4, R1.Pin_1
  N3: Mod1.GND, S1.Pin_1, S1.Pin_2
