# Fritzing sketch senspr_circuit (saved by Fritzing 0.9.9b)
breadboards: 1

parts:
  Mod1 = Raspberry Pi 4B
  Part1 = 9 Degrees of Freedom - Sensor Stick

nets:
  3V3: Mod1.3V3, Part1.VCC
  N1: Mod1.GPIO2, Part1.SDA
  N2: Mod1.GPIO3, Part1.SCL
  GND: Mod1.GND, Part1.GND
